// Logisim project decode.circ as structural Verilog
module decode (
  input  [23:0] instru
);

  // alu_registry alu_registry_1: pin names not known
endmodule
